// Logisim project makp2.circ as structural Verilog: 1 circuit, main circuit main
module main (
  input  in_1,
  input  in_2,
  input  in_3
);

  wire ALUSrc, and_1_out, and_3_out, and_7_out, and_8_out, and_9_out, and_10_out, and_11_out, and_12_out,
       auipc, Branch, CLK, clock_1_out, comparator_1_eq, comparator_1_gt, comparator_1_lt, comparator_2_eq,
       comparator_2_gt, comparator_2_lt, demultiplexer_2_out0, demultiplexer_2_out1, demultiplexer_2_out2,
       demultiplexer_2_out4, demultiplexer_2_out5, demultiplexer_3_out0, demultiplexer_3_out4,
       demultiplexer_4_out0, demultiplexer_4_out1, demultiplexer_4_out2, demultiplexer_5_out0,
       demultiplexer_5_out1, demultiplexer_5_out2, demultiplexer_5_out3, demultiplexer_6_out0,
       demultiplexer_6_out1, demultiplexer_6_out2, demultiplexer_6_out3, demultiplexer_7_out1,
       demultiplexer_7_out2, demultiplexer_7_out3, demultiplexer_7_out4, demultiplexer_7_out5,
       demultiplexer_7_out6, demultiplexer_7_out7, demultiplexer_7_out8, demultiplexer_7_out9,
       demultiplexer_7_out10, demultiplexer_7_out11, demultiplexer_7_out12, demultiplexer_7_out13,
       demultiplexer_7_out14, demultiplexer_7_out15, demultiplexer_7_out16, demultiplexer_7_out17,
       demultiplexer_7_out18, demultiplexer_7_out19, demultiplexer_7_out20, demultiplexer_7_out21,
       demultiplexer_7_out22, demultiplexer_7_out23, demultiplexer_7_out24, demultiplexer_7_out25,
       demultiplexer_7_out26, demultiplexer_7_out27, demultiplexer_7_out28, demultiplexer_7_out29,
       demultiplexer_7_out30, demultiplexer_7_out31, jalr, Jump, keyboard_1_avail, lui, MemRead, MemWrite,
       nor_1_out, not_1_out, not_2_out, not_3_out, not_4_out, not_5_out, not_6_out, not_7_out, not_8_out,
       or_1_out, or_2_out, or_3_out, or_4_out, or_5_out, or_6_out, or_7_out, or_8_out, or_9_out, or_10_out,
       or_12_out, or_13_out, RegWrite;
  wire [1:0] controlled_buffer_6_out, demultiplexer_1_out0, multiplexer_5_out, multiplexer_6_out;
  wire [2:0] f3;
  wire [3:0] multiplexer_15_out, rom_2_data, rom_3_data;
  wire [4:0] multiplexer_24_out, rd, rs1, rs2;
  wire [6:0] bit_extender_1_out, f7, keyboard_1_data, multiplexer_1_out;
  wire [7:0] multiplexer_8_out, multiplexer_9_out, multiplexer_10_out, multiplexer_11_out,
       multiplexer_18_out, multiplexer_19_out, multiplexer_20_out, multiplexer_21_out, ram_1_dout,
       ram_2_dout, ram_3_dout, ram_4_dout;
  wire [10:6] rom_1_data;
  wire [21:0] adder_2_out, bit_extender_2_out, demultiplexer_1_out0_2, multiplexer_12_out,
       multiplexer_13_out, multiplexer_14_out;
  wire [23:0] adder_1_out, demultiplexer_1_out1, multiplexer_2_out, multiplexer_3_out, PC, PCNext,
       subtractor_1_out;
  wire [24:0] multiplexer_4_out;
  wire [31:0] adder_3_out, ALUOut, and_13_out, bit_extender_3_out, bit_extender_4_out, bit_extender_5_out,
       bit_extender_6_out, bit_extender_7_out, bit_extender_8_out, bit_extender_9_out, bit_extender_10_out,
       bit_extender_11_out, bit_extender_12_out, bit_extender_13_out, bit_extender_14_out,
       bit_extender_15_out, bit_extender_16_out, bit_extender_17_out, bit_extender_18_out,
       controlled_buffer_1_out, controlled_buffer_4_out, Imm, IR, multiplexer_16_out, multiplexer_23_out,
       multiplexer_25_out, or_11_out, RAMOut, reg1, reg2, shifter_1_out, shifter_2_out, shifter_3_out,
       subtractor_3_out, x1_q, x2_q, x3_q, x4_q, x5_q, x6_q, x7_q, x8_q, x9_q, x10_q, x11_q, x12_q, x13_q,
       x14_q, x15_q, x16_q, x17_q, x18_q, x19_q, x20_q, x21_q, x22_q, x23_q, x24_q, x25_q, x26_q, x27_q,
       x28_q, x29_q, x30_q, x31_q, xor_1_out;

  or or_1 (or_1_out, and_1_out, Jump);
  Clock clock_1 (.out(clock_1_out));
  Subtractor #(.width(24)) subtractor_1 (.a(Imm[23:0]), .b(24'h4), .out(subtractor_1_out));  // open: bin, bout
  and and_1 (and_1_out, Branch, ALUOut[0]);
  or or_2 (or_2_out, or_1_out, jalr);
  not not_1 (not_1_out, CLK);
  Multiplexer #(.width(32)) multiplexer_1 (
    .in0(32'h33), .in1(IR), .out({f7, rs2, rs1, f3, rd, multiplexer_1_out}), .sel(CLK));
  Multiplexer #(.width(24)) multiplexer_2 (.in0(adder_1_out), .in1(ALUOut[23:0]), .out(multiplexer_2_out), .sel(jalr));
  and and_2 (CLK, in_3, clock_1_out);
  or or_3 (or_3_out, CLK, and_3_out);
  and and_3 (and_3_out, or_2_out, not_1_out);
  Multiplexer #(.width(24)) multiplexer_3 (
    .in0(24'h4), .in1(subtractor_1_out), .out(multiplexer_3_out), .sel(or_1_out));
  Register #(.width(24)) register_1 (.D(multiplexer_2_out), .clk(or_3_out), .Q(PCNext), .clr(in_1));  // open: en
  Adder #(.width(24)) adder_1 (.a(multiplexer_3_out), .b(PCNext), .out(adder_1_out));  // open: cin, cout
  Subtractor #(.width(24)) subtractor_2 (.a(PCNext), .b(24'h4), .out(PC));  // open: bin, bout
  ROM #(.addrWidth(5), .dataWidth(11)) rom_1 (
    .addr(multiplexer_1_out[6:2]), .data({rom_1_data, Jump, Branch, MemWrite, MemRead, ALUSrc, RegWrite}));
  or or_4 (or_4_out, MemRead, MemWrite);
  and and_4 (auipc, ~multiplexer_1_out[6], ~multiplexer_1_out[5], multiplexer_1_out[4], ~multiplexer_1_out[3], multiplexer_1_out[2]);  // AND_Gate
  and and_5 (lui, ~multiplexer_1_out[6], multiplexer_1_out[5], multiplexer_1_out[4], ~multiplexer_1_out[3], multiplexer_1_out[2]);  // AND_Gate
  and and_6 (jalr, multiplexer_1_out[6], multiplexer_1_out[5], ~multiplexer_1_out[4], ~multiplexer_1_out[3], multiplexer_1_out[2]);  // AND_Gate
  Multiplexer #(.width(25)) multiplexer_4 (
    .in0({1'b0, PCNext}), .in1(ALUOut[24:0]), .out(multiplexer_4_out), .sel(or_4_out));
  not not_2 (not_2_out, multiplexer_4_out[24]);
  and and_7 (and_7_out, not_2_out, MemWrite);
  and and_8 (and_8_out, MemWrite, multiplexer_4_out[24]);
  Demultiplexer #(.width(24)) demultiplexer_1 (
    .out0({demultiplexer_1_out0_2, demultiplexer_1_out0}), .out1(demultiplexer_1_out1),
    .in(multiplexer_4_out[23:0]), .sel(multiplexer_4_out[24]));
  Multiplexer #(.width(2)) multiplexer_5 (.in0(2'b10), .in1(f3[1:0]), .out(multiplexer_5_out), .sel(MemWrite));
  Multiplexer #(.width(2)) multiplexer_6 (.in0(2'b00), .in1({f7[5], f7[0]}), .out(multiplexer_6_out), .sel(or_5_out));
  or or_5 (or_5_out, and_10_out, not_4_out);
  not not_3 (not_3_out, CLK);
  Demultiplexer #(.select(3)) demultiplexer_2 (
    .out0(demultiplexer_2_out0), .out1(demultiplexer_2_out1), .out2(demultiplexer_2_out2),
    .out4(demultiplexer_2_out4), .out5(demultiplexer_2_out5), .in(not_3_out), .sel(demultiplexer_1_out1[4:2]));  // open: out3, out6, out7
  Demultiplexer #(.select(3)) demultiplexer_3 (
    .out0(demultiplexer_3_out0), .out4(demultiplexer_3_out4), .in(and_8_out), .sel(demultiplexer_1_out1[4:2]));  // open: out1, out2, out3, out5, out6, out7
  Demultiplexer #(.select(2)) demultiplexer_4 (
    .out0(demultiplexer_4_out0), .out1(demultiplexer_4_out1), .out2(demultiplexer_4_out2), .in(and_7_out),
    .sel(multiplexer_5_out));  // open: out3
  and and_9 (and_9_out, ~rom_1_data[6], rom_1_data[7]);  // AND_Gate
  not not_4 (not_4_out, and_9_out);
  Bit_Extender #(.in_width(32), .out_width(7)) bit_extender_1 (.in(reg2), .out(bit_extender_1_out));
  TTY #(.cols(38), .rows(16)) tty_1 (
    .data(bit_extender_1_out), .clk(demultiplexer_2_out0), .we(demultiplexer_3_out0),
    .clr(demultiplexer_2_out1));
  Demultiplexer #(.select(2)) demultiplexer_5 (
    .out0(demultiplexer_5_out0), .out1(demultiplexer_5_out1), .out2(demultiplexer_5_out2),
    .out3(demultiplexer_5_out3), .in(demultiplexer_4_out1), .sel(demultiplexer_1_out0));
  Demultiplexer #(.select(2)) demultiplexer_6 (
    .out0(demultiplexer_6_out0), .out1(demultiplexer_6_out1), .out2(demultiplexer_6_out2),
    .out3(demultiplexer_6_out3), .in(demultiplexer_4_out0), .sel(demultiplexer_1_out0));
  and and_10 (and_10_out, and_9_out, or_6_out);
  or or_6 (or_6_out, and_11_out, and_12_out);
  and and_11 (and_11_out, f3[0], ~f3[1], f3[2]);  // AND_Gate
  and and_12 (and_12_out, f3[0], ~f3[1], ~f3[2]);  // AND_Gate
  Bit_Extender #(.in_width(32), .out_width(22)) bit_extender_2 (.in(reg2), .out(bit_extender_2_out));
  Adder #(.width(22)) adder_2 (.a(demultiplexer_1_out0_2), .b(22'h1), .out(adder_2_out));  // open: cin, cout
  assign bit_extender_3_out = {{20{f7[6]}}, {f7, rs2}};  // Bit_Extender bit_extender_3
  assign bit_extender_4_out = {{20{f7[6]}}, {f7, rd}};  // Bit_Extender bit_extender_4
  assign bit_extender_5_out = {{19{f7[6]}}, {f7[6], rd[0], f7[5:0], rd[4:1], 1'b0}};  // Bit_Extender bit_extender_5
  assign bit_extender_6_out = {{11{f7[6]}}, {f7[6], rs1, f3, rs2[0], f7[5:0], rs2[4:1], 1'b0}};  // Bit_Extender bit_extender_6
  ROM #(.addrWidth(5), .dataWidth(4)) rom_2 (.addr({multiplexer_6_out, f3}), .data(rom_2_data));
  ROM #(.addrWidth(3), .dataWidth(4)) rom_3 (.addr(f3), .data(rom_3_data));
  // RGB_Video #(.cursor("No Cursor")) rgb_video_1: pin names not known; wires that end beside it: demultiplexer_2_out5, demultiplexer_2_out4, demultiplexer_3_out4, bit_extender_2_out[6:0], bit_extender_2_out[13:7], bit_extender_2_out[21:14]
  Multiplexer #(.select(3), .width(32)) multiplexer_7 (
    .in0(bit_extender_3_out), .in1(bit_extender_4_out), .in2(bit_extender_5_out),
    .in3({f7, rs2, rs1, f3, {12{1'b0}}}), .in4(bit_extender_6_out), .out(Imm), .sel(rom_1_data[10:8]));  // open: in5, in6, in7
  Keyboard keyboard_1 (.clk(demultiplexer_2_out2), .avail(keyboard_1_avail), .data(keyboard_1_data));  // open: re, clr
  Multiplexer #(.select(2), .width(8)) multiplexer_8 (
    .in0(reg2[7:0]), .in1(reg2[31:24]), .in2(reg2[23:16]), .in3(reg2[15:8]), .out(multiplexer_8_out),
    .sel(demultiplexer_1_out0));
  Multiplexer #(.select(2), .width(8)) multiplexer_9 (
    .in0(reg2[15:8]), .in1(reg2[7:0]), .in2(reg2[31:24]), .in3(reg2[23:16]), .out(multiplexer_9_out),
    .sel(demultiplexer_1_out0));
  Multiplexer #(.select(2), .width(8)) multiplexer_10 (
    .in0(reg2[23:16]), .in1(reg2[15:8]), .in2(reg2[7:0]), .in3(reg2[31:24]), .out(multiplexer_10_out),
    .sel(demultiplexer_1_out0));
  Multiplexer #(.select(2), .width(8)) multiplexer_11 (
    .in0(reg2[31:24]), .in1(reg2[23:16]), .in2(reg2[15:8]), .in3(reg2[7:0]), .out(multiplexer_11_out),
    .sel(demultiplexer_1_out0));
  Multiplexer #(.select(2), .width(22)) multiplexer_12 (
    .in0(demultiplexer_1_out0_2), .in1(adder_2_out), .in2(adder_2_out), .in3(adder_2_out),
    .out(multiplexer_12_out), .sel(demultiplexer_1_out0));
  Multiplexer #(.select(2), .width(22)) multiplexer_13 (
    .in0(demultiplexer_1_out0_2), .in1(demultiplexer_1_out0_2), .in2(adder_2_out), .in3(adder_2_out),
    .out(multiplexer_13_out), .sel(demultiplexer_1_out0));
  Multiplexer #(.select(2), .width(22)) multiplexer_14 (
    .in0(demultiplexer_1_out0_2), .in1(demultiplexer_1_out0_2), .in2(demultiplexer_1_out0_2),
    .in3(adder_2_out), .out(multiplexer_14_out), .sel(demultiplexer_1_out0));
  assign bit_extender_7_out = {{25{1'b0}}, keyboard_1_data};  // Bit_Extender bit_extender_7
  assign bit_extender_8_out = {{31{1'b0}}, keyboard_1_avail};  // Bit_Extender bit_extender_8
  assign controlled_buffer_1_out = not_5_out ? reg2 : 32'bz;  // Controlled_Buffer controlled_buffer_1
  Multiplexer #(.select(2), .width(4)) multiplexer_15 (
    .in0(4'b0000), .in1(rom_2_data), .in2(rom_2_data), .in3(rom_3_data), .out(multiplexer_15_out),
    .sel(rom_1_data[7:6]));
  or or_7 (or_7_out, demultiplexer_4_out2, demultiplexer_5_out0, demultiplexer_5_out3, demultiplexer_6_out0);
  or or_8 (or_8_out, demultiplexer_4_out2, demultiplexer_5_out0, demultiplexer_5_out1, demultiplexer_6_out1);
  or or_9 (or_9_out, demultiplexer_4_out2, demultiplexer_5_out1, demultiplexer_5_out2, demultiplexer_6_out2);
  or or_10 (or_10_out, demultiplexer_4_out2, demultiplexer_5_out2, demultiplexer_5_out3, demultiplexer_6_out3);
  not not_5 (not_5_out, ALUSrc);
  assign controlled_buffer_1_out = ALUSrc ? Imm : 32'bz;  // Controlled_Buffer controlled_buffer_2
  Multiplexer #(.select(3), .width(32)) multiplexer_16 (
    .in2(bit_extender_7_out), .in3(bit_extender_8_out), .out(multiplexer_16_out),
    .sel(demultiplexer_1_out1[4:2]));  // open: in0, in1, in4, in5, in6, in7
  RAM #(.addrWidth(22), .asyncread("true"), .trigger("falling")) ram_1 (
    .addr(multiplexer_12_out), .we(or_7_out), .oe(1'b1), .clk(CLK), .din(multiplexer_8_out), .dout(ram_1_dout));
  RAM #(.addrWidth(22), .asyncread("true"), .trigger("falling")) ram_2 (
    .addr(multiplexer_13_out), .we(or_8_out), .oe(1'b1), .clk(CLK), .din(multiplexer_9_out), .dout(ram_2_dout));
  RAM #(.addrWidth(22), .asyncread("true"), .trigger("falling")) ram_3 (
    .addr(multiplexer_14_out), .we(or_9_out), .oe(1'b1), .clk(CLK), .din(multiplexer_10_out),
    .dout(ram_3_dout));
  RAM #(.addrWidth(22), .asyncread("true"), .trigger("falling")) ram_4 (
    .addr(demultiplexer_1_out0_2), .we(or_10_out), .oe(1'b1), .clk(CLK), .din(multiplexer_11_out),
    .dout(ram_4_dout));
  assign reg1 = auipc ? {{8{1'b0}}, PC} : 32'bz;  // Controlled_Buffer controlled_buffer_3
  assign controlled_buffer_4_out = multiplexer_4_out[24] ? multiplexer_16_out : 32'bz;  // Controlled_Buffer controlled_buffer_4
  Adder #(.width(32)) adder_3 (.a(reg1), .b(controlled_buffer_1_out), .out(adder_3_out));  // open: cin, cout
  Subtractor #(.width(32)) subtractor_3 (
    .a(reg1), .b(controlled_buffer_1_out), .out(subtractor_3_out));  // open: bin, bout
  assign and_13_out = reg1 & controlled_buffer_1_out;  // AND_Gate and_13, 32 bits wide
  assign or_11_out = reg1 | controlled_buffer_1_out;  // OR_Gate or_11, 32 bits wide
  assign xor_1_out = reg1 ^ controlled_buffer_1_out;  // XOR_Gate xor_1, 32 bits wide
  Shifter #(.width(32)) shifter_1 (.in(reg1), .\dist (controlled_buffer_1_out[4:0]), .out(shifter_1_out));
  Shifter #(.shift("lr"), .width(32)) shifter_2 (.in(reg1), .\dist (controlled_buffer_1_out[4:0]), .out(shifter_2_out));
  Shifter #(.shift("ar"), .width(32)) shifter_3 (.in(reg1), .\dist (controlled_buffer_1_out[4:0]), .out(shifter_3_out));
  or or_12 (or_12_out, comparator_1_gt, comparator_1_eq);
  not not_6 (not_6_out, comparator_1_eq);
  Comparator #(.width(32)) comparator_1 (
    .a(reg1), .b(controlled_buffer_1_out), .gt(comparator_1_gt), .eq(comparator_1_eq), .lt(comparator_1_lt));
  or or_13 (or_13_out, comparator_2_gt, comparator_2_eq);
  Comparator #(.mode("unsigned"), .width(32)) comparator_2 (
    .a(reg1), .b(controlled_buffer_1_out), .gt(comparator_2_gt), .eq(comparator_2_eq), .lt(comparator_2_lt));
  assign bit_extender_9_out = {{31{1'b0}}, or_12_out};  // Bit_Extender bit_extender_9
  assign bit_extender_10_out = {{31{1'b0}}, not_6_out};  // Bit_Extender bit_extender_10
  assign bit_extender_11_out = {{31{1'b0}}, comparator_1_eq};  // Bit_Extender bit_extender_11
  assign bit_extender_12_out = {{31{1'b0}}, comparator_1_lt};  // Bit_Extender bit_extender_12
  assign bit_extender_13_out = {{31{1'b0}}, or_13_out};  // Bit_Extender bit_extender_13
  assign bit_extender_14_out = {{31{1'b0}}, comparator_2_lt};  // Bit_Extender bit_extender_14
  Multiplexer #(.select(4), .width(32)) multiplexer_17 (
    .in0(adder_3_out), .in1(subtractor_3_out), .in2(and_13_out), .in3(or_11_out), .in4(xor_1_out),
    .in5(shifter_1_out), .in6(shifter_2_out), .in7(shifter_3_out), .in8(bit_extender_11_out),
    .in9(bit_extender_10_out), .in10(bit_extender_9_out), .in11(bit_extender_13_out),
    .in12(bit_extender_12_out), .in13(bit_extender_14_out), .out(ALUOut), .sel(multiplexer_15_out));  // open: in14, in15
  Multiplexer #(.select(2), .width(8)) multiplexer_18 (
    .in0(ram_1_dout), .in1(ram_2_dout), .in2(ram_3_dout), .in3(ram_4_dout), .out(multiplexer_18_out),
    .sel(demultiplexer_1_out0));
  Multiplexer #(.select(2), .width(8)) multiplexer_19 (
    .in0(ram_2_dout), .in1(ram_3_dout), .in2(ram_4_dout), .in3(ram_1_dout), .out(multiplexer_19_out),
    .sel(demultiplexer_1_out0));
  Multiplexer #(.select(2), .width(8)) multiplexer_20 (
    .in0(ram_3_dout), .in1(ram_4_dout), .in2(ram_1_dout), .in3(ram_2_dout), .out(multiplexer_20_out),
    .sel(demultiplexer_1_out0));
  Multiplexer #(.select(2), .width(8)) multiplexer_21 (
    .in0(ram_4_dout), .in1(ram_1_dout), .in2(ram_2_dout), .in3(ram_3_dout), .out(multiplexer_21_out),
    .sel(demultiplexer_1_out0));
  Register #(.width(32)) register_2 (.D(controlled_buffer_4_out), .clk(CLK), .Q(IR), .clr(in_2));  // open: en
  assign bit_extender_15_out = {{24{controlled_buffer_4_out[7]}}, controlled_buffer_4_out[7:0]};  // Bit_Extender bit_extender_15
  assign bit_extender_16_out = {{16{controlled_buffer_4_out[15]}}, controlled_buffer_4_out[15:0]};  // Bit_Extender bit_extender_16
  assign bit_extender_17_out = {{24{1'b0}}, controlled_buffer_4_out[7:0]};  // Bit_Extender bit_extender_17
  assign bit_extender_18_out = {{16{1'b0}}, controlled_buffer_4_out[15:0]};  // Bit_Extender bit_extender_18
  Multiplexer #(.select(3), .width(32)) multiplexer_22 (
    .in0(bit_extender_15_out), .in1(bit_extender_16_out), .in2(controlled_buffer_4_out),
    .in4(bit_extender_17_out), .in5(bit_extender_18_out), .out(RAMOut), .sel(f3));  // open: in3, in6, in7
  assign controlled_buffer_4_out = not_2_out ? {multiplexer_21_out, multiplexer_20_out, multiplexer_19_out, multiplexer_18_out} : 32'bz;  // Controlled_Buffer controlled_buffer_5
  assign controlled_buffer_6_out = MemRead ? 2'b01 : 2'bz;  // Controlled_Buffer controlled_buffer_6
  assign controlled_buffer_6_out = Jump ? 2'b10 : 2'bz;  // Controlled_Buffer controlled_buffer_7
  assign controlled_buffer_6_out = lui ? 2'b11 : 2'bz;  // Controlled_Buffer controlled_buffer_8
  Multiplexer #(.select(2), .width(32)) multiplexer_23 (
    .in0(ALUOut), .in1(RAMOut), .in2({{8{1'b0}}, PCNext}), .in3(Imm), .out(multiplexer_23_out),
    .sel(controlled_buffer_6_out));
  assign controlled_buffer_6_out = nor_1_out ? 2'b00 : 2'bz;  // Controlled_Buffer controlled_buffer_9
  nor nor_1 (nor_1_out, MemRead, Jump, lui);
  Demultiplexer #(.select(5)) demultiplexer_7 (
    .out1(demultiplexer_7_out1), .out2(demultiplexer_7_out2), .out3(demultiplexer_7_out3),
    .out4(demultiplexer_7_out4), .out5(demultiplexer_7_out5), .out6(demultiplexer_7_out6),
    .out7(demultiplexer_7_out7), .out8(demultiplexer_7_out8), .out9(demultiplexer_7_out9),
    .out10(demultiplexer_7_out10), .out11(demultiplexer_7_out11), .out12(demultiplexer_7_out12),
    .out13(demultiplexer_7_out13), .out14(demultiplexer_7_out14), .out15(demultiplexer_7_out15),
    .out16(demultiplexer_7_out16), .out17(demultiplexer_7_out17), .out18(demultiplexer_7_out18),
    .out19(demultiplexer_7_out19), .out20(demultiplexer_7_out20), .out21(demultiplexer_7_out21),
    .out22(demultiplexer_7_out22), .out23(demultiplexer_7_out23), .out24(demultiplexer_7_out24),
    .out25(demultiplexer_7_out25), .out26(demultiplexer_7_out26), .out27(demultiplexer_7_out27),
    .out28(demultiplexer_7_out28), .out29(demultiplexer_7_out29), .out30(demultiplexer_7_out30),
    .out31(demultiplexer_7_out31), .in(1'b1), .sel(multiplexer_24_out));  // open: out0
  Multiplexer #(.width(5)) multiplexer_24 (.in0({5{1'b0}}), .in1(rd), .out(multiplexer_24_out), .sel(RegWrite));
  not not_7 (not_7_out, CLK);
  Register #(.width(32)) x31 (
    .D(multiplexer_23_out), .en(demultiplexer_7_out31), .clk(not_7_out), .Q(x31_q));  // open: clr
  Register #(.width(32)) x30 (
    .D(multiplexer_23_out), .en(demultiplexer_7_out30), .clk(not_7_out), .Q(x30_q));  // open: clr
  Register #(.width(32)) x29 (
    .D(multiplexer_23_out), .en(demultiplexer_7_out29), .clk(not_7_out), .Q(x29_q));  // open: clr
  Register #(.width(32)) x28 (
    .D(multiplexer_23_out), .en(demultiplexer_7_out28), .clk(not_7_out), .Q(x28_q));  // open: clr
  Register #(.width(32)) x27 (
    .D(multiplexer_23_out), .en(demultiplexer_7_out27), .clk(not_7_out), .Q(x27_q));  // open: clr
  Register #(.width(32)) x26 (
    .D(multiplexer_23_out), .en(demultiplexer_7_out26), .clk(not_7_out), .Q(x26_q));  // open: clr
  Register #(.width(32)) x25 (
    .D(multiplexer_23_out), .en(demultiplexer_7_out25), .clk(not_7_out), .Q(x25_q));  // open: clr
  Register #(.width(32)) x24 (
    .D(multiplexer_23_out), .en(demultiplexer_7_out24), .clk(not_7_out), .Q(x24_q));  // open: clr
  Register #(.width(32)) x23 (
    .D(multiplexer_23_out), .en(demultiplexer_7_out23), .clk(not_7_out), .Q(x23_q));  // open: clr
  Register #(.width(32)) x22 (
    .D(multiplexer_23_out), .en(demultiplexer_7_out22), .clk(not_7_out), .Q(x22_q));  // open: clr
  Register #(.width(32)) x21 (
    .D(multiplexer_23_out), .en(demultiplexer_7_out21), .clk(not_7_out), .Q(x21_q));  // open: clr
  Register #(.width(32)) x20 (
    .D(multiplexer_23_out), .en(demultiplexer_7_out20), .clk(not_7_out), .Q(x20_q));  // open: clr
  Register #(.width(32)) x19 (
    .D(multiplexer_23_out), .en(demultiplexer_7_out19), .clk(not_7_out), .Q(x19_q));  // open: clr
  Register #(.width(32)) x18 (
    .D(multiplexer_23_out), .en(demultiplexer_7_out18), .clk(not_7_out), .Q(x18_q));  // open: clr
  Register #(.width(32)) x17 (
    .D(multiplexer_23_out), .en(demultiplexer_7_out17), .clk(not_7_out), .Q(x17_q));  // open: clr
  Register #(.width(32)) x16 (
    .D(multiplexer_23_out), .en(demultiplexer_7_out16), .clk(not_7_out), .Q(x16_q));  // open: clr
  Register #(.width(32)) x15 (
    .D(multiplexer_23_out), .en(demultiplexer_7_out15), .clk(not_7_out), .Q(x15_q));  // open: clr
  Register #(.width(32)) x14 (
    .D(multiplexer_23_out), .en(demultiplexer_7_out14), .clk(not_7_out), .Q(x14_q));  // open: clr
  Register #(.width(32)) x13 (
    .D(multiplexer_23_out), .en(demultiplexer_7_out13), .clk(not_7_out), .Q(x13_q));  // open: clr
  Register #(.width(32)) x12 (
    .D(multiplexer_23_out), .en(demultiplexer_7_out12), .clk(not_7_out), .Q(x12_q));  // open: clr
  Register #(.width(32)) x11 (
    .D(multiplexer_23_out), .en(demultiplexer_7_out11), .clk(not_7_out), .Q(x11_q));  // open: clr
  Register #(.width(32)) x10 (
    .D(multiplexer_23_out), .en(demultiplexer_7_out10), .clk(not_7_out), .Q(x10_q));  // open: clr
  Register #(.width(32)) x9 (
    .D(multiplexer_23_out), .en(demultiplexer_7_out9), .clk(not_7_out), .Q(x9_q));  // open: clr
  Register #(.width(32)) x8 (
    .D(multiplexer_23_out), .en(demultiplexer_7_out8), .clk(not_7_out), .Q(x8_q));  // open: clr
  Register #(.width(32)) x7 (
    .D(multiplexer_23_out), .en(demultiplexer_7_out7), .clk(not_7_out), .Q(x7_q));  // open: clr
  Register #(.width(32)) x6 (
    .D(multiplexer_23_out), .en(demultiplexer_7_out6), .clk(not_7_out), .Q(x6_q));  // open: clr
  Register #(.width(32)) x5 (
    .D(multiplexer_23_out), .en(demultiplexer_7_out5), .clk(not_7_out), .Q(x5_q));  // open: clr
  Register #(.width(32)) x4 (
    .D(multiplexer_23_out), .en(demultiplexer_7_out4), .clk(not_7_out), .Q(x4_q));  // open: clr
  Register #(.width(32)) x3 (
    .D(multiplexer_23_out), .en(demultiplexer_7_out3), .clk(not_7_out), .Q(x3_q));  // open: clr
  Register #(.width(32)) x2 (
    .D(multiplexer_23_out), .en(demultiplexer_7_out2), .clk(not_7_out), .Q(x2_q));  // open: clr
  Register #(.width(32)) x1 (
    .D(multiplexer_23_out), .en(demultiplexer_7_out1), .clk(not_7_out), .Q(x1_q));  // open: clr
  not not_8 (not_8_out, auipc);
  Multiplexer #(.select(5), .width(32)) multiplexer_25 (
    .in0({32{1'b0}}), .in1(x1_q), .in2(x2_q), .in3(x3_q), .in4(x4_q), .in5(x5_q), .in6(x6_q), .in7(x7_q),
    .in8(x8_q), .in9(x9_q), .in10(x10_q), .in11(x11_q), .in12(x12_q), .in13(x13_q), .in14(x14_q),
    .in15(x15_q), .in16(x16_q), .in17(x17_q), .in18(x18_q), .in19(x19_q), .in20(x20_q), .in21(x21_q),
    .in22(x22_q), .in23(x23_q), .in24(x24_q), .in25(x25_q), .in26(x26_q), .in27(x27_q), .in28(x28_q),
    .in29(x29_q), .in30(x30_q), .in31(x31_q), .out(multiplexer_25_out), .sel(rs1));
  assign reg1 = not_8_out ? multiplexer_25_out : 32'bz;  // Controlled_Buffer controlled_buffer_10
  Multiplexer #(.select(5), .width(32)) multiplexer_26 (
    .in0({32{1'b0}}), .in1(x1_q), .in2(x2_q), .in3(x3_q), .in4(x4_q), .in5(x5_q), .in6(x6_q), .in7(x7_q),
    .in8(x8_q), .in9(x9_q), .in10(x10_q), .in11(x11_q), .in12(x12_q), .in13(x13_q), .in14(x14_q),
    .in15(x15_q), .in16(x16_q), .in17(x17_q), .in18(x18_q), .in19(x19_q), .in20(x20_q), .in21(x21_q),
    .in22(x22_q), .in23(x23_q), .in24(x24_q), .in25(x25_q), .in26(x26_q), .in27(x27_q), .in28(x28_q),
    .in29(x29_q), .in30(x30_q), .in31(x31_q), .out(reg2), .sel(rs2));

  // Notes on the sheet:
  //   ValGen Unit
  //   contents of rom_1 (hex, n*v repeats v):
  //   7 0 0 0 83 303 0 0 10a 0 0 0 41 303 10*0 2d0 23 0 421
  //   ImmGen Unit
  //   contents of rom_2 (hex, n*v repeats v):
  //   0 5 c d 4 6 3 2 8*0 1 4*0 7
  //   contents of rom_3 (hex, n*v repeats v):
  //   8 9 0 0 c a d b
  //   ACU
endmodule
